# Fritzing sketch mainboard_rf433mhz_toy_car (saved by Fritzing 0.9.3b)
circuit board: 13.684cm x 10.6783cm

parts:
  Part1 = Arduino Uno (Rev3) - ICSP
  U1 = L298_BRIDGE_DRIVER [package=powerso20]
  M2 = DC Motor [part_number=DC1]
  Rx1 = mystery part, 4 pins [chip_label=RF_Reciever]
  OLED_I2C2 = OLED 128x64 I2C Monochrome Display
  M3 = DC Motor [part_number=DC2]
  BAT2 = BC9VPC [part_number=BAT2_9V package=bc9vpc]
  VCC1 = Battery [part_number=BAT1_37V_LI_ION]
  Part2 = SRF05 Ultrasonic Rangefinder [part_number=sensor_front]
  Part3 = SRF05 Ultrasonic Rangefinder [part_number=sensor_back]

nets:
  VCC: Part1.5V, Rx1.pin4, OLED_I2C2.VDD, Part2.VCC, Part3.VCC
  GND: Part1.GND, U1.GND, U1.VS, U1.VSS, Rx1.pin1, OLED_I2C2.GND, BAT2.V-, VCC1.-, Part2.GND, Part3.GND
  N1: Part1.D9_PWM, Part2.Trig
  N2: Part1.D10_PWM/SS, Part2.Echo
  N3: Part1.D11_PWM/MOSI, Part3.Trig
  N4: Part1.D12/MISO, Part3.Echo
  N5: Part1.A4/SDA, OLED_I2C2.SDA
  N6: Part1.A5/SCL, OLED_I2C2.SCK
  N7: Part1.D2, Rx1.pin2
  N8: Part1.D4, U1.IN1
  N9: Part1.D5_PWM, U1.IN2
  N10: Part1.D6_PWM, U1.IN3
  N11: Part1.D7, U1.IN4
  N12: Part1.VIN, BAT2.V+
  N13: U1.SENSE_A, VCC1.+
  N14: U1.OUT1, M2.pin_1
  N15: U1.OUT2, M2.pin_2
  N16: U1.OUT3, M3.pin_2
  N17: U1.OUT4, M3.pin_1

notes:
  Note: OUT1/2 and OUT3/4 are connnected in the same way.
  OUT1/OUT3 can be either DC+ or DC-.
  DC1:
  IN1 (Direction)
  IN2 (Speed PWM)
  DC2:
  IN3 (Speed PWM)
  IN4 (Direction)
  Assume: SENSE_A is the 12V input pin
  Two 3.7V Li-ION Batteries (7.4V to SENSE_A)
  1-GND
  2-DATA
  3-DATA
  4-VCC
  Author : Michael Li
  Date: 10/1/2017
  Project: RC Toy Car
  Design: Toy Car Main Module with RF Reciever
  Company: Self
  Rev: A
