# Fritzing sketch remote_rf433mhz_toy_car (saved by Fritzing 0.9.3b)
circuit board: 15.6774cm x 8.33924cm
breadboards: 1

parts:
  Part2 = Arduino Nano (Rev3.0) (ICSP)
  OLED_I2C1 = OLED 128x64 I2C Monochrome Display
  Tx1 = mystery part, 3 pins [chip_label=?]
  Part3 = Adafruit Analog 2-Axis Joystick [part_number="Adafruit #512"]
  BAT1 = BC9VPC [package=bc9vpc]

nets:
  GND: Part2.GND, OLED_I2C1.GND, Tx1.pin1, Part3.GND, BAT1.V-
  N1: Part2.D3, Part3.SWITCH
  N2: Part2.VIN, BAT1.V+
  5V: Part2.5V, OLED_I2C1.VDD, Tx1.pin2, Part3.VCC
  N3: Part2.A7, Part3.XOUT
  N4: Part2.A6, Part3.YOUT
  N5: Part2.A5, OLED_I2C1.SCK
  N6: Part2.A4, OLED_I2C1.SDA
  N7: Part2.D13/SCK, Tx1.pin3

notes:
  RF Transmitter
  Arduino Nano
  XY Joy Stick
  Y - speed/direction
  X - no turn or left turn or right turn
  9V Battery
  433Mhz RF Transmitter
  1-GND
  2-VCC
  3-DATA
  Author : Michael Li
  Date: 10/1/2017
  Project: RC Toy Car
  Design: Toy Car's Remote Control Module with RF Transmitter
  Company: Self
  Rev: A

custom parts:
  Adafruit Analog 2-Axis Joystick: This mini-kit makes it easy to mount a PSP/Xbox-like thumb joystick to your project. The thumbstick is an analog joystick - more accurate and sensitive than just 'directional' joysticks - with a 'press in to select' button. Since it's analog, you'll need two analog reading pins on your microcontroller to determine X and Y. Having an extra digital input will let you read the switch. The pack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
